// Logisim project BellBox(8-bit computer).circ as structural Verilog: 21 circuits, main circuit customcpu 
// Enable
module customcpu (
  input  [7:0] INPUT_BUS,
  input  Enable,
  input  Load,
  input  [7:0] INCANDDEC,
  input  [2:0] in_5,
  input  in_6,
  input  Enable_2,
  input  Load_2,
  input  Enable_3,
  input  Load_3,
  output [7:0] STORED_VALUE,
  output [7:0] ALU_OUTPUT,
  output Z,
  output NF,
  output OF,
  output C,
  output [3:0] Dec,
  output [3:0] ins,
  output [7:0] STORED_VALUE_2
);

  // _8bitinstructionregister 8bitinstructionregister_1: pin names not known; wires that end beside it: INPUT_BUS, Enable_2, Load_2, Dec, ins
  _8bitregister u_8bitregister_1 (
    .in_1(INPUT_BUS), .Enable(Enable), .Load(Load), ._8BitOutput(STORED_VALUE));  // open: I8, I7, I6, I5, I4, I3, I2, I1
  ALU alu_1 (
    .A(STORED_VALUE), .B(STORED_VALUE_2), .Controlbit(in_5), .zero(Z), .enable(in_6), .negative_flag(NF),
    .overflow_flag(OF), .carry(C), .Output(ALU_OUTPUT), .incanddec(INCANDDEC));
  _8bitregister u_8bitregister_2 (
    .in_1(INPUT_BUS), .Enable(Enable_3), .Load(Load_3), ._8BitOutput(STORED_VALUE_2));  // open: I8, I7, I6, I5, I4, I3, I2, I1

  // Notes on the sheet:
  //   Instruction Register
  //   A
  //   B
endmodule

module FullAdder (
  input  in_1,
  input  in_2,
  input  in_3,
  output Sum,
  output out_5
);

  wire and_1_out, and_2_out, xor_1_out;

  xor xor_1 (xor_1_out, in_1, in_2);
  and and_1 (and_1_out, in_1, in_2);
  xor xor_2 (Sum, xor_1_out, in_3);
  and and_2 (and_2_out, in_3, xor_1_out);
  or or_1 (out_5, and_2_out, and_1_out);
endmodule

module ALU (
  input  [7:0] A,
  input  [7:0] B,
  input  [2:0] Controlbit,
  input  enable,
  input  [7:0] incanddec,
  output zero,
  output [7:0] Output,
  output negative_flag,
  output overflow_flag,
  output carry
);

  wire adder_1_cout, adder_2_cout, subtractor_1_bout, subtractor_2_bout;
  wire [6:0] multiplexer_1_out;
  wire [7:0] adder_1_out, adder_2_out, AND_out, NOT_out, OR_out, subtractor_1_out, subtractor_2_out, XOR_out;

  Adder adder_1 (.a(A), .b(B), .out(adder_1_out), .cout(adder_1_cout));  // open: cin
  Subtractor subtractor_1 (.a(A), .b(B), .out(subtractor_1_out), .bout(subtractor_1_bout));  // open: bin
  assign AND_out = A & B;  // AND_Gate AND, 8 bits wide
  assign OR_out = A | B;  // OR_Gate OR, 8 bits wide
  assign NOT_out = ~A;  // NOT_Gate NOT, 8 bits wide
  Adder adder_2 (.a(A), .b(incanddec), .out(adder_2_out), .cout(adder_2_cout));  // open: cin
  Subtractor subtractor_2 (.a(A), .b(incanddec), .out(subtractor_2_out), .bout(subtractor_2_bout));  // open: bin
  assign XOR_out = A ^ B;  // XOR_Gate XOR, 8 bits wide
  Multiplexer #(.select(3), .width(8), .enable("false")) multiplexer_1 (
    .in0(adder_1_out), .in1(subtractor_1_out), .in2(AND_out), .in3(OR_out), .in4(NOT_out), .in5(adder_2_out),
    .in6(subtractor_2_out), .in7(XOR_out), .out({negative_flag, multiplexer_1_out}), .sel(Controlbit));
  nor nor_1 (zero, multiplexer_1_out[0], multiplexer_1_out[1], multiplexer_1_out[2], multiplexer_1_out[3], multiplexer_1_out[4], multiplexer_1_out[5], multiplexer_1_out[6], negative_flag);
  ExactlyOne xor_2 (.out(overflow_flag), .in0(negative_flag), .in1(B[7]), .in2(A[7]));
  or or_2 (carry, subtractor_1_bout, adder_1_cout, adder_2_cout, subtractor_2_bout);
  assign Output[7] = enable ? negative_flag : 1'bz;  // Controlled_Buffer controlled_buffer_1
  assign Output[2] = enable ? multiplexer_1_out[2] : 1'bz;  // Controlled_Buffer controlled_buffer_2
  assign Output[3] = enable ? multiplexer_1_out[3] : 1'bz;  // Controlled_Buffer controlled_buffer_3
  assign Output[4] = enable ? multiplexer_1_out[4] : 1'bz;  // Controlled_Buffer controlled_buffer_4
  assign Output[5] = enable ? multiplexer_1_out[5] : 1'bz;  // Controlled_Buffer controlled_buffer_5
  assign Output[6] = enable ? multiplexer_1_out[6] : 1'bz;  // Controlled_Buffer controlled_buffer_6
  assign Output[0] = enable ? multiplexer_1_out[0] : 1'bz;  // Controlled_Buffer controlled_buffer_7
  assign Output[1] = enable ? multiplexer_1_out[1] : 1'bz;  // Controlled_Buffer controlled_buffer_8

  // Notes on the sheet:
  //   Incrementer
  //   Decrementor
endmodule

module Adder8bit (
  input  [7:0] A,
  input  Carry_In,
  input  [7:0] B,
  output [7:0] Sum,
  output out_5
);

  wire fulladder_1_out_5, fulladder_2_out_5, fulladder_3_out_5, fulladder_4_out_5, fulladder_5_out_5,
       fulladder_6_out_5, fulladder_7_out_5;

  FullAdder fulladder_1 (.in_1(A[0]), .in_2(B[0]), .in_3(Carry_In), .Sum(Sum[0]), .out_5(fulladder_1_out_5));
  FullAdder fulladder_2 (.in_1(A[1]), .in_2(B[1]), .in_3(fulladder_1_out_5), .Sum(Sum[1]), .out_5(fulladder_2_out_5));
  FullAdder fulladder_3 (.in_1(A[2]), .in_2(B[2]), .in_3(fulladder_2_out_5), .Sum(Sum[2]), .out_5(fulladder_3_out_5));
  FullAdder fulladder_4 (.in_1(A[3]), .in_2(B[3]), .in_3(fulladder_3_out_5), .Sum(Sum[3]), .out_5(fulladder_4_out_5));
  FullAdder fulladder_5 (.in_1(A[4]), .in_2(B[4]), .in_3(fulladder_4_out_5), .Sum(Sum[4]), .out_5(fulladder_5_out_5));
  FullAdder fulladder_6 (.in_1(A[5]), .in_2(B[5]), .in_3(fulladder_5_out_5), .Sum(Sum[5]), .out_5(fulladder_6_out_5));
  FullAdder fulladder_7 (.in_1(A[6]), .in_2(B[6]), .in_3(fulladder_6_out_5), .Sum(Sum[6]), .out_5(fulladder_7_out_5));
  FullAdder fulladder_8 (.in_1(A[7]), .in_2(B[7]), .in_3(fulladder_7_out_5), .Sum(Sum[7]), .out_5(out_5));
endmodule

module Subtractor8bit (
  input  [7:0] A,
  input  [7:0] B,
  output [7:0] Diff
);

  Subtractor subtractor_1 (.a(A), .b(B), .out(Diff));  // open: bin, bout
endmodule

module Final (
  input  carry,
  input  load,
  input  [3:0] addressinputdirect,
  input  addressmuxenable,
  input  [7:0] incdec,
  input  [2:0] CB,
  input  [7:0] datainputdirect,
  input  [3:0] in_8,
  input  [3:0] in_9,
  input  in_10,
  output [3:0] out_11,
  output [7:0] OutputofRam,
  output [3:0] addregisterputput,
  output [7:0] Output,
  output [7:0] Output_2,
  output [7:0] Output_3,
  output Z,
  output NF,
  output OF,
  output C,
  output [7:0] dataregisteroutput,
  output [7:0] Output_4,
  output [7:0] Output_5,
  output [3:0] for_decoder,
  output [3:0] out_25,
  output [3:0] out_26,
  output [2:0] out_27,
  output out_28,
  output [6:0] dataregisteroutput_2
);

  wire and_1_out, and_2_out, Clear_2_out, clear_out, clock_1_out, controlled_buffer_12_out, decoder_1_out0,
       decoder_1_out1, decoder_1_out2, decoder_1_out3, decoder_1_out4, decoder_1_out5, decoder_1_out6,
       decoder_1_out7, empy_instruction_1_out_3, not_1_out, not_2_out, not_3_out, not_4_out, not_5_out,
       not_6_out, not_7_out, not_8_out, not_9_out, or_1_out, or_3_out;
  wire [3:0] n8bitbinarydecode_1_output1, n8bitbinarydecode_1_output2, n8bitbinarydecode_1_output3,
       register_1_q;
  wire [7:0] output_registser_q, register_2_q, rom_1_data, rom_2_data;

  not not_1 (not_1_out, controlled_buffer_12_out);
  Register #(.width(4)) register_1 (
    .D(Output_2[3:0]), .en(rom_1_data[6]), .Q(register_1_q), .clk(controlled_buffer_12_out), .clr(Clear_2_out));
  Button clear (.out(clear_out));
  Counter #(.width(3), .max('h7)) counter_1 (
    .load(1'b0), .count(1'b1), .Q(dataregisteroutput_2[2:0]), .carry(out_28), .clk(not_1_out), .clr(or_1_out));  // open: D
  Register register_2 (
    .D(Output_2), .en(controlled_buffer_12_out), .Q(register_2_q), .clk(controlled_buffer_12_out),
    .clr(Clear_2_out));
  Register register_3 (
    .D(OutputofRam), .en(rom_1_data[2]), .Q({out_26, for_decoder}), .clk(controlled_buffer_12_out),
    .clr(Clear_2_out));
  Decoder #(.select(3)) decoder_1 (
    .out0(decoder_1_out0), .out1(decoder_1_out1), .out2(decoder_1_out2), .out3(decoder_1_out3),
    .out4(decoder_1_out4), .out5(decoder_1_out5), .out6(decoder_1_out6), .out7(decoder_1_out7),
    .sel(dataregisteroutput_2[2:0]));  // open: en
  or or_1 (or_1_out, decoder_1_out6, Clear_2_out);
  Multiplexer #(.width(4)) multiplexer_1 (
    .in0(register_1_q), .in1(addressinputdirect), .out(addregisterputput), .sel(addressmuxenable));  // open: en
  not not_2 (not_2_out, decoder_1_out3);
  not not_3 (not_3_out, decoder_1_out4);
  not not_4 (not_4_out, decoder_1_out5);
  ROM #(.addrWidth(7)) rom_1 (.addr(dataregisteroutput_2), .data(rom_1_data), .sel(1'b1));
  Multiplexer #(.width(8)) multiplexer_2 (
    .in0(register_2_q), .in1(datainputdirect), .out(dataregisteroutput), .sel(addressmuxenable));  // open: en
  assign Output_2[3] = rom_1_data[3] ? for_decoder[3] : 1'bz;  // Controlled_Buffer controlled_buffer_1
  assign out_25[0] = rom_1_data[3] ? out_26[0] : 1'bz;  // Controlled_Buffer controlled_buffer_2
  assign out_25[1] = rom_1_data[3] ? out_26[1] : 1'bz;  // Controlled_Buffer controlled_buffer_3
  assign out_25[2] = rom_1_data[3] ? out_26[2] : 1'bz;  // Controlled_Buffer controlled_buffer_4
  assign out_25[3] = rom_1_data[3] ? out_26[3] : 1'bz;  // Controlled_Buffer controlled_buffer_5
  DotMatrix #(.matrixcols(6), .matrixrows(1), .dotshape("circle")) dotmatrix_1 (
    .col0(not_5_out), .col1(not_6_out), .col2(not_7_out), .col3(not_2_out), .col4(not_3_out), .col5(not_4_out));
  not not_5 (not_5_out, decoder_1_out0);
  not not_6 (not_6_out, decoder_1_out1);
  not not_7 (not_7_out, decoder_1_out2);
  assign Output_2 = rom_1_data[4] ? OutputofRam : 8'bz;  // Controlled_Buffer controlled_buffer_6
  RAM #(.addrWidth(4), .bus("separate")) ram_1 (
    .addr(addregisterputput), .din(dataregisteroutput), .data(OutputofRam), .str(or_3_out), .sel(1'b1),
    .clk(controlled_buffer_12_out), .ld(rom_1_data[4]), .clr(clear_out));
  assign Output_2[0] = rom_1_data[3] ? for_decoder[0] : 1'bz;  // Controlled_Buffer controlled_buffer_7
  assign Output_2[1] = rom_1_data[3] ? for_decoder[1] : 1'bz;  // Controlled_Buffer controlled_buffer_8
  assign Output_2[2] = rom_1_data[3] ? for_decoder[2] : 1'bz;  // Controlled_Buffer controlled_buffer_9
  and and_1 (and_1_out, not_5_out, not_6_out);
  empy_instruction empy_instruction_1 (
    .in_1(rom_1_data), .in_2({{2{rom_2_data[7]}}, rom_2_data[5:0]}), .out_3(empy_instruction_1_out_3));
  ROM #(.addrWidth(7)) rom_2 (.addr(dataregisteroutput_2), .data({{2{rom_2_data[7]}}, rom_2_data[5:0]}), .sel(1'b1));
  assign Output_2[7] = rom_2_data[0] ? 1'b0 : 1'bz;  // Controlled_Buffer controlled_buffer_10
  RAM #(.addrWidth(4), .bus("separate")) ram_2 (
    .addr(addregisterputput), .din(dataregisteroutput), .data(OutputofRam), .str(or_3_out), .sel(1'b1),
    .clk(controlled_buffer_12_out), .ld(rom_1_data[4]), .clr(clear_out));
  // OR_Gate or_2 has open pins: in0=empy_instruction_1_out_3, in1=and_1_out, out=open
  Multiplexer #(.width(4)) multiplexer_3 (
    .in0(in_8), .in1(out_26), .out(dataregisteroutput_2[6:3]), .sel(and_1_out));  // open: en
  DotMatrix #(.matrixcols(8), .matrixrows(1), .dotshape("circle")) dotmatrix_2 (
    .col0(Output_2[7]), .col1(Output_2[6]), .col2(Output_2[5]), .col3(Output_2[4]), .col4(Output_2[3]),
    .col5(Output_2[2]), .col6(Output_2[1]), .col7(Output_2[0]));
  assign Output_2 = and_2_out ? Output_3 : 8'bz;  // Controlled_Buffer controlled_buffer_11
  and and_2 (and_2_out, not_9_out, rom_1_data[0]);
  Clock clock_1 (.out(clock_1_out));
  not not_8 (not_8_out, rom_1_data[7]);
  not not_9 (not_9_out, rom_2_data[5]);
  LED MI (.in(rom_1_data[6]));
  LED Halt (.in(rom_1_data[7]));
  Button Clear_2 (.out(Clear_2_out));
  assign controlled_buffer_12_out = not_8_out ? clock_1_out : 1'bz;  // Controlled_Buffer controlled_buffer_12
  LED RI (.in(or_3_out));
  LED RO (.in(rom_1_data[4]));
  ALU alu_1 (
    .A(Output_3), .B(Output_5), .Controlbit(CB), .zero(Z), .enable(rom_2_data[5]), .negative_flag(NF),
    .overflow_flag(OF), .carry(C), .Output(Output_2), .incanddec(incdec));
  Register output_registser (
    .D(Output_2), .en(rom_2_data[2]), .Q(output_registser_q), .clk(controlled_buffer_12_out),
    .clr(Clear_2_out));
  LED II (.in(rom_1_data[2]));
  LED AI (.in(rom_1_data[1]));
  LED IO (.in(rom_1_data[3]));
  or or_3 (or_3_out, rom_1_data[5], in_10);
  assign Output_2[3:0] = rom_2_data[0] ? out_11 : 4'bz;  // Controlled_Buffer controlled_buffer_13
  Register register_4 (.D(Output_2), .en(rom_1_data[1]), .Q(Output), .clk(controlled_buffer_12_out), .clr(Clear_2_out));
  Register register_5 (
    .D(Output_2), .en(rom_2_data[4]), .Q(Output_4), .clk(controlled_buffer_12_out), .clr(Clear_2_out));
  _8bitbinarydecode u_8bitbinarydecode_1 (
    .output1(n8bitbinarydecode_1_output1), .output2(n8bitbinarydecode_1_output2),
    .output3(n8bitbinarydecode_1_output3), .\input (output_registser_q));
  LED AO (.in(rom_1_data[0]));
  LED aluO (.in(rom_2_data[5]));
  LED BI (.in(rom_2_data[4]));
  LED BO (.in(rom_2_data[3]));
  LED DO (.in(rom_2_data[2]));
  Program_counter program_counter_1 (
    .load(load), .count_enable(rom_2_data[1]), .clock(controlled_buffer_12_out), .clear(Clear_2_out),
    .carry(carry), .\output (out_11));  // open: input
  assign Output_3[6] = rom_1_data[0] ? Output[6] : 1'bz;  // Controlled_Buffer controlled_buffer_14
  assign Output_3[7] = rom_1_data[0] ? Output[7] : 1'bz;  // Controlled_Buffer controlled_buffer_15
  assign Output_5[6] = rom_2_data[3] ? Output_4[6] : 1'bz;  // Controlled_Buffer controlled_buffer_16
  assign Output_5[7] = rom_2_data[3] ? Output_4[7] : 1'bz;  // Controlled_Buffer controlled_buffer_17
  Hex_Digit_Display hex_digit_display_1 (.value(n8bitbinarydecode_1_output3));  // open: dp
  LED PCE (.in(rom_2_data[1]));
  LED PCO (.in(rom_2_data[0]));
  assign Output_3[1] = rom_1_data[0] ? Output[1] : 1'bz;  // Controlled_Buffer controlled_buffer_18
  assign Output_3[2] = rom_1_data[0] ? Output[2] : 1'bz;  // Controlled_Buffer controlled_buffer_19
  assign Output_3[3] = rom_1_data[0] ? Output[3] : 1'bz;  // Controlled_Buffer controlled_buffer_20
  assign Output_3[4] = rom_1_data[0] ? Output[4] : 1'bz;  // Controlled_Buffer controlled_buffer_21
  assign Output_3[5] = rom_1_data[0] ? Output[5] : 1'bz;  // Controlled_Buffer controlled_buffer_22
  assign Output_5[1] = rom_2_data[3] ? Output_4[1] : 1'bz;  // Controlled_Buffer controlled_buffer_23
  assign Output_5[2] = rom_2_data[3] ? Output_4[2] : 1'bz;  // Controlled_Buffer controlled_buffer_24
  assign Output_5[3] = rom_2_data[3] ? Output_4[3] : 1'bz;  // Controlled_Buffer controlled_buffer_25
  assign Output_5[4] = rom_2_data[3] ? Output_4[4] : 1'bz;  // Controlled_Buffer controlled_buffer_26
  assign Output_5[5] = rom_2_data[3] ? Output_4[5] : 1'bz;  // Controlled_Buffer controlled_buffer_27
  Hex_Digit_Display hex_digit_display_2 (.value(n8bitbinarydecode_1_output2));  // open: dp
  Hex_Digit_Display hex_digit_display_3 (.value(n8bitbinarydecode_1_output1));  // open: dp
  assign Output_3[0] = rom_1_data[0] ? Output[0] : 1'bz;  // Controlled_Buffer controlled_buffer_28
  assign Output_5[0] = rom_2_data[3] ? Output_4[0] : 1'bz;  // Controlled_Buffer controlled_buffer_29

  assign out_27 = dataregisteroutput_2[2:0];
  // also tied to GND on the sheet: {decoder_1_out7, rom_2_data[7]}

  // Notes on the sheet:
  //   contents of rom_1 (hex, n*v repeats v):
  //   40 14 6*0 40 14 48 12 4*0 40 12 48 10 3 0 0 0 80 87*0 40 14 1 7*0 80
  //   contents of rom_2 (hex, n*v repeats v):
  //   1 2 6*0 1 2 6*0 1 2 0 10 28 91*0 1 2 4
endmodule

module d_flip_flop (
  input  in_1,
  output out_2,
  output out_3
);

  wire clock_1_out, nand_1_out, nand_2_out, not_1_out;

  Clock #(.highDuration(2), .lowDuration(2)) clock_1 (.out(clock_1_out));
  not not_1 (not_1_out, in_1);
  nand nand_1 (nand_1_out, in_1, clock_1_out);
  nand nand_2 (nand_2_out, not_1_out, clock_1_out);
  nand nand_3 (out_2, nand_1_out, out_3);
  nand nand_4 (out_3, out_2, nand_2_out);
endmodule

module _1bitregister (
  input  load,
  input  data,
  input  enable,
  output out_4,
  output out_5
);

  wire and_1_out, and_2_out, d_flip_flop_1_out_2, not_1_out, or_1_out;

  not not_1 (not_1_out, load);
  and and_1 (and_1_out, d_flip_flop_1_out_2, not_1_out);
  and and_2 (and_2_out, load, data);
  or or_1 (or_1_out, and_1_out, and_2_out);
  d_flip_flop d_flip_flop_1 (.in_1(or_1_out), .out_2(d_flip_flop_1_out_2), .out_3(out_5));
  and and_3 (out_4, d_flip_flop_1_out_2, enable);

  // Notes on the sheet:
  //   D-flip flop
  //   Trisate Buffer
endmodule

// Register
module _8bitregister (
  input  [7:0] in_1,
  input  Enable,
  input  Load,
  output I8,
  output I7,
  output I6,
  output [7:0] _8BitOutput,
  output I5,
  output I4,
  output I3,
  output I2,
  output I1
);

  _1bitregister u_1bitregister_1 (.load(Load), .data(in_1[7]), .enable(Enable), .out_4(_8BitOutput[7]));  // open: out_5
  _1bitregister u_1bitregister_2 (.load(Load), .data(in_1[6]), .enable(Enable), .out_4(_8BitOutput[6]));  // open: out_5
  _1bitregister u_1bitregister_3 (.load(Load), .data(in_1[5]), .enable(Enable), .out_4(_8BitOutput[5]));  // open: out_5
  _1bitregister u_1bitregister_4 (.load(Load), .data(in_1[4]), .enable(Enable), .out_4(_8BitOutput[4]));  // open: out_5
  _1bitregister u_1bitregister_5 (.load(Load), .data(in_1[3]), .enable(Enable), .out_4(_8BitOutput[3]));  // open: out_5
  _1bitregister u_1bitregister_6 (.load(Load), .data(in_1[2]), .enable(Enable), .out_4(_8BitOutput[2]));  // open: out_5
  _1bitregister u_1bitregister_7 (.load(Load), .data(in_1[1]), .enable(Enable), .out_4(_8BitOutput[1]));  // open: out_5
  _1bitregister u_1bitregister_8 (.load(Load), .data(in_1[0]), .enable(Enable), .out_4(_8BitOutput[0]));  // open: out_5

  assign I1 = _8BitOutput[0];
  assign I2 = _8BitOutput[1];
  assign I3 = _8BitOutput[2];
  assign I4 = _8BitOutput[3];
  assign I5 = _8BitOutput[4];
  assign I6 = _8BitOutput[5];
  assign I7 = _8BitOutput[6];
  assign I8 = _8BitOutput[7];
endmodule

module _8bitinstructionregister (
  input  in_1,
  input  [7:0] in_2,
  input  load,
  input  clear,
  input  enable,
  output [3:0] for_decoder,
  output [3:0] out_7
);

  wire [7:0] register_1_q;

  Register register_1 (.D(in_2), .en(load), .Q(register_1_q), .clk(in_1), .clr(clear));
  assign for_decoder[3] = enable ? register_1_q[3] : 1'bz;  // Controlled_Buffer controlled_buffer_1
  assign out_7[0] = enable ? register_1_q[4] : 1'bz;  // Controlled_Buffer controlled_buffer_2
  assign out_7[1] = enable ? register_1_q[5] : 1'bz;  // Controlled_Buffer controlled_buffer_3
  assign out_7[2] = enable ? register_1_q[6] : 1'bz;  // Controlled_Buffer controlled_buffer_4
  assign out_7[3] = enable ? register_1_q[7] : 1'bz;  // Controlled_Buffer controlled_buffer_5
  assign for_decoder[0] = enable ? register_1_q[0] : 1'bz;  // Controlled_Buffer controlled_buffer_6
  assign for_decoder[1] = enable ? register_1_q[1] : 1'bz;  // Controlled_Buffer controlled_buffer_7
  assign for_decoder[2] = enable ? register_1_q[2] : 1'bz;  // Controlled_Buffer controlled_buffer_8
endmodule

module semi8bitregister (
  input  [7:0] \input ,
  input  load,
  input  clear,
  input  enable,
  output [7:0] Output
);

  wire clock_1_out;
  wire [7:0] register_1_q;

  Register register_1 (.D(\input ), .en(load), .Q(register_1_q), .clk(clock_1_out), .clr(clear));
  Clock clock_1 (.out(clock_1_out));
  assign Output[6] = enable ? register_1_q[6] : 1'bz;  // Controlled_Buffer controlled_buffer_1
  assign Output[7] = enable ? register_1_q[7] : 1'bz;  // Controlled_Buffer controlled_buffer_2
  assign Output[1] = enable ? register_1_q[1] : 1'bz;  // Controlled_Buffer controlled_buffer_3
  assign Output[2] = enable ? register_1_q[2] : 1'bz;  // Controlled_Buffer controlled_buffer_4
  assign Output[3] = enable ? register_1_q[3] : 1'bz;  // Controlled_Buffer controlled_buffer_5
  assign Output[4] = enable ? register_1_q[4] : 1'bz;  // Controlled_Buffer controlled_buffer_6
  assign Output[5] = enable ? register_1_q[5] : 1'bz;  // Controlled_Buffer controlled_buffer_7
  assign Output[0] = enable ? register_1_q[0] : 1'bz;  // Controlled_Buffer controlled_buffer_8
endmodule

module rammodule (
  input  addregisterenble,
  input  [3:0] addressinputregister,
  input  [3:0] addressinputdirect,
  input  addressmuxenable,
  input  storevalueintotheram,
  input  loadvaluetooutput,
  input  dataregisterenable,
  input  [7:0] datainputregister,
  input  datamuxenable,
  input  [7:0] datainputdirect,
  output [3:0] addregisterputput,
  output [7:0] OutputofRam,
  output [7:0] dataregisteroutput
);

  wire clear_out, clock_out;
  wire [3:0] register_1_q;
  wire [7:0] register_2_q;

  Clock clock (.out(clock_out));
  Register #(.width(4)) register_1 (
    .D(addressinputregister), .en(addregisterenble), .Q(register_1_q), .clk(clock_out));  // open: clr
  Button clear (.out(clear_out));
  Multiplexer #(.width(4)) multiplexer_1 (
    .in0(register_1_q), .in1(addressinputdirect), .out(addregisterputput), .sel(addressmuxenable));  // open: en
  Register register_2 (.D(datainputregister), .en(dataregisterenable), .Q(register_2_q), .clk(clock_out));  // open: clr
  Multiplexer #(.width(8)) multiplexer_2 (
    .in0(register_2_q), .in1(datainputdirect), .out(dataregisteroutput), .sel(datamuxenable));  // open: en
  RAM #(.addrWidth(4), .bus("separate")) ram_1 (
    .addr(addregisterputput), .din(dataregisteroutput), .data(OutputofRam), .str(storevalueintotheram),
    .sel(1'b1), .clk(clock_out), .ld(loadvaluetooutput), .clr(clear_out));
  RAM #(.addrWidth(4), .bus("separate")) ram_2 (
    .addr(addregisterputput), .din(dataregisteroutput), .data(OutputofRam), .str(storevalueintotheram),
    .sel(1'b1), .clk(clock_out), .ld(loadvaluetooutput), .clr(clear_out));
endmodule

// program counter
module Program_counter (
  input  load,
  input  [3:0] \input ,
  input  count_enable,
  input  clock,
  input  clear,
  output [3:0] \output ,
  output carry
);

  Counter #(.width(4), .max('hf)) counter_1 (
    .load(load), .D(\input ), .count(count_enable), .Q(\output ), .carry(carry), .clk(clock), .clr(clear));
endmodule

module _7segment_hex_decoder (
  input  D,
  input  C,
  input  B,
  input  A,
  output a_2,
  output b_2,
  output c_2,
  output d_2,
  output e,
  output f,
  output g
);

  wire nand_1_out, nand_2_out, nand_3_out, nand_4_out, nand_5_out, nand_6_out, nand_7_out, nand_8_out,
       nand_9_out, nand_10_out, nand_11_out, nand_12_out, nand_13_out, nand_14_out, nand_15_out, nand_16_out,
       nand_17_out, nand_18_out, nand_19_out, nand_20_out, nand_21_out, nand_22_out, nand_23_out,
       nand_24_out, nand_25_out, nand_26_out, nand_27_out, nand_28_out, nand_29_out, nand_30_out,
       nand_31_out, nand_32_out, nand_33_out, nand_34_out, nand_35_out, nand_36_out, nand_37_out,
       nand_38_out, nand_39_out, nand_40_out, nand_41_out, nand_42_out, nand_43_out, nand_44_out,
       nand_45_out, nand_46_out, nand_47_out, nand_48_out, nand_49_out, nand_50_out, nand_51_out,
       nand_52_out, nand_53_out, nand_54_out, nand_55_out, nand_56_out, nand_57_out, nand_58_out,
       nand_59_out, nand_60_out, nand_61_out, nand_62_out, nand_63_out, nand_64_out, nand_65_out,
       nand_66_out, nand_67_out, nand_68_out, nand_69_out, nand_70_out, nand_71_out, nand_72_out,
       nand_73_out, nand_74_out, nand_75_out, nand_76_out, nand_77_out, nand_78_out, nand_79_out,
       nand_80_out, nand_81_out, nand_82_out, nand_83_out, nand_84_out, nand_85_out, nand_86_out,
       nand_87_out, nand_88_out, nand_89_out, nand_90_out, nand_91_out, nand_92_out, nand_93_out,
       nand_94_out, nand_95_out, nand_96_out, nand_97_out, nand_98_out, nand_99_out, nand_100_out,
       nand_101_out, nand_102_out, nand_103_out, nand_104_out, nand_106_out, nand_107_out, nand_108_out,
       nand_109_out, nand_110_out, nand_111_out, nand_112_out, nand_113_out, nand_114_out, nand_115_out,
       nand_116_out, nand_117_out, nand_118_out, nand_119_out, nand_120_out, nand_121_out, nand_122_out,
       nand_123_out, nand_124_out, nand_125_out, nand_126_out, nand_127_out, nand_128_out, nand_129_out,
       nand_130_out, nand_131_out, nand_132_out, nand_133_out, nand_134_out, nand_136_out, nand_137_out,
       nand_138_out, nand_139_out, nand_141_out, nand_142_out, nand_143_out, nand_144_out, nand_145_out,
       nand_146_out, nand_147_out, nand_148_out;

  nand nand_1 (nand_1_out, C, C);
  nand nand_2 (nand_2_out, D, D);
  nand nand_3 (nand_3_out, B, B);
  nand nand_4 (nand_4_out, D, D);
  nand nand_5 (nand_5_out, B, B);
  nand nand_6 (nand_6_out, D, D);
  nand nand_7 (nand_7_out, D, D);
  nand nand_8 (nand_8_out, C, C);
  nand nand_9 (nand_9_out, C, C);
  nand nand_10 (nand_10_out, C, C);
  nand nand_11 (nand_11_out, A, A);
  nand nand_12 (nand_12_out, A, A);
  nand nand_13 (nand_13_out, D, D);
  nand nand_14 (nand_14_out, C, C);
  nand nand_15 (nand_15_out, A, A);
  nand nand_16 (nand_16_out, D, D);
  nand nand_17 (nand_17_out, D, nand_1_out);
  nand nand_18 (nand_18_out, nand_2_out, nand_3_out);
  nand nand_19 (nand_19_out, nand_4_out, nand_5_out);
  nand nand_20 (nand_20_out, nand_6_out, A);
  nand nand_21 (nand_21_out, nand_7_out, nand_8_out);
  nand nand_22 (nand_22_out, nand_9_out, B);
  nand nand_23 (nand_23_out, nand_10_out, nand_11_out);
  nand nand_24 (nand_24_out, B, nand_12_out);
  nand nand_25 (nand_25_out, D, B);
  nand nand_26 (nand_26_out, D, C);
  nand nand_27 (nand_27_out, nand_13_out, C);
  nand nand_28 (nand_28_out, nand_14_out, B);
  nand nand_29 (nand_29_out, B, nand_15_out);
  nand nand_30 (nand_30_out, nand_16_out, C);
  nand nand_31 (nand_31_out, C, C);
  nand nand_32 (nand_32_out, A, A);
  nand nand_33 (nand_33_out, D, D);
  nand nand_34 (nand_34_out, D, D);
  nand nand_35 (nand_35_out, nand_17_out, nand_17_out);
  nand nand_36 (nand_36_out, B, B);
  nand nand_37 (nand_37_out, D, D);
  nand nand_38 (nand_38_out, C, C);
  nand nand_39 (nand_39_out, nand_18_out, nand_18_out);
  nand nand_40 (nand_40_out, A, A);
  nand nand_41 (nand_41_out, D, D);
  nand nand_42 (nand_42_out, B, B);
  nand nand_43 (nand_43_out, nand_19_out, nand_20_out);
  nand nand_44 (nand_44_out, B, B);
  nand nand_45 (nand_45_out, D, D);
  nand nand_46 (nand_46_out, C, C);
  nand nand_47 (nand_47_out, nand_21_out, nand_21_out);
  nand nand_48 (nand_48_out, A, A);
  nand nand_49 (nand_49_out, nand_22_out, nand_22_out);
  nand nand_50 (nand_50_out, B, B);
  nand nand_51 (nand_51_out, B, B);
  nand nand_52 (nand_52_out, nand_23_out, nand_24_out);
  nand nand_53 (nand_53_out, nand_25_out, nand_26_out);
  nand nand_54 (nand_54_out, B, B);
  nand nand_55 (nand_55_out, A, A);
  nand nand_56 (nand_56_out, nand_27_out, nand_27_out);
  nand nand_57 (nand_57_out, B, B);
  nand nand_58 (nand_58_out, nand_28_out, nand_29_out);
  nand nand_59 (nand_59_out, nand_30_out, nand_30_out);
  nand nand_60 (nand_60_out, B, B);
  nand nand_61 (nand_61_out, C, C);
  nand nand_62 (nand_62_out, nand_31_out, nand_32_out);
  nand nand_63 (nand_63_out, nand_33_out, B);
  nand nand_64 (nand_64_out, nand_34_out, C);
  nand nand_65 (nand_65_out, C, B);
  nand nand_66 (nand_66_out, nand_35_out, nand_36_out);
  nand nand_67 (nand_67_out, nand_37_out, nand_38_out);
  nand nand_68 (nand_68_out, nand_39_out, nand_40_out);
  nand nand_69 (nand_69_out, nand_41_out, B);
  nand nand_70 (nand_70_out, D, nand_42_out);
  nand nand_71 (nand_71_out, nand_43_out, nand_43_out);
  nand nand_72 (nand_72_out, nand_44_out, A);
  nand nand_73 (nand_73_out, nand_45_out, C);
  nand nand_74 (nand_74_out, D, nand_46_out);
  nand nand_75 (nand_75_out, nand_47_out, nand_48_out);
  nand nand_76 (nand_76_out, nand_49_out, A);
  nand nand_77 (nand_77_out, C, nand_50_out);
  nand nand_78 (nand_78_out, C, B);
  nand nand_79 (nand_79_out, D, nand_51_out);
  nand nand_80 (nand_80_out, nand_52_out, nand_52_out);
  nand nand_81 (nand_81_out, nand_53_out, nand_53_out);
  nand nand_82 (nand_82_out, nand_54_out, nand_55_out);
  nand nand_83 (nand_83_out, nand_56_out, nand_57_out);
  nand nand_84 (nand_84_out, nand_58_out, nand_58_out);
  nand nand_85 (nand_85_out, nand_59_out, nand_60_out);
  nand nand_86 (nand_86_out, D, nand_61_out);
  nand nand_87 (nand_87_out, D, A);
  nand nand_88 (nand_88_out, nand_62_out, nand_63_out);
  nand nand_89 (nand_89_out, nand_64_out, nand_64_out);
  nand nand_90 (nand_90_out, nand_65_out, nand_66_out);
  nand nand_91 (nand_91_out, A, A);
  nand nand_92 (nand_92_out, nand_67_out, nand_68_out);
  nand nand_93 (nand_93_out, C, C);
  nand nand_94 (nand_94_out, A, A);
  nand nand_95 (nand_95_out, nand_69_out, nand_69_out);
  nand nand_96 (nand_96_out, nand_70_out, nand_70_out);
  nand nand_97 (nand_97_out, nand_71_out, nand_72_out);
  nand nand_98 (nand_98_out, nand_73_out, nand_74_out);
  nand nand_99 (nand_99_out, nand_75_out, nand_76_out);
  nand nand_100 (nand_100_out, nand_77_out, nand_77_out);
  nand nand_101 (nand_101_out, nand_78_out, nand_78_out);
  nand nand_102 (nand_102_out, A, A);
  nand nand_103 (nand_103_out, nand_79_out, nand_79_out);
  nand nand_104 (nand_104_out, A, A);
  nand nand_105 (e, nand_80_out, nand_81_out);
  nand nand_106 (nand_106_out, nand_82_out, nand_83_out);
  nand nand_107 (nand_107_out, A, A);
  nand nand_108 (nand_108_out, C, C);
  nand nand_109 (nand_109_out, nand_84_out, nand_85_out);
  nand nand_110 (nand_110_out, nand_86_out, nand_87_out);
  nand nand_111 (nand_111_out, nand_88_out, nand_88_out);
  nand nand_112 (nand_112_out, nand_89_out, A);
  nand nand_113 (nand_113_out, nand_90_out, nand_90_out);
  nand nand_114 (nand_114_out, D, nand_91_out);
  nand nand_115 (nand_115_out, nand_92_out, nand_92_out);
  nand nand_116 (nand_116_out, nand_93_out, nand_94_out);
  nand nand_117 (nand_117_out, nand_95_out, A);
  nand nand_118 (nand_118_out, nand_96_out, A);
  nand nand_119 (nand_119_out, nand_97_out, nand_97_out);
  nand nand_120 (nand_120_out, nand_98_out, nand_98_out);
  nand nand_121 (nand_121_out, nand_99_out, nand_99_out);
  nand nand_122 (nand_122_out, nand_100_out, A);
  nand nand_123 (nand_123_out, nand_101_out, nand_102_out);
  nand nand_124 (nand_124_out, nand_103_out, nand_104_out);
  nand nand_125 (nand_125_out, nand_106_out, nand_106_out);
  nand nand_126 (nand_126_out, C, nand_107_out);
  nand nand_127 (nand_127_out, D, nand_108_out);
  nand nand_128 (nand_128_out, D, B);
  nand nand_129 (nand_129_out, nand_109_out, nand_109_out);
  nand nand_130 (nand_130_out, nand_110_out, nand_110_out);
  nand nand_131 (nand_131_out, nand_111_out, nand_112_out);
  nand nand_132 (nand_132_out, nand_113_out, nand_114_out);
  nand nand_133 (nand_133_out, nand_115_out, nand_116_out);
  nand nand_134 (nand_134_out, nand_117_out, nand_118_out);
  nand nand_135 (c_2, nand_119_out, nand_120_out);
  nand nand_136 (nand_136_out, nand_121_out, nand_122_out);
  nand nand_137 (nand_137_out, nand_123_out, nand_124_out);
  nand nand_138 (nand_138_out, nand_125_out, nand_126_out);
  nand nand_139 (nand_139_out, nand_127_out, nand_128_out);
  nand nand_140 (g, nand_129_out, nand_130_out);
  nand nand_141 (nand_141_out, nand_131_out, nand_131_out);
  nand nand_142 (nand_142_out, nand_132_out, nand_132_out);
  nand nand_143 (nand_143_out, nand_133_out, nand_133_out);
  nand nand_144 (nand_144_out, nand_134_out, nand_134_out);
  nand nand_145 (nand_145_out, nand_136_out, nand_136_out);
  nand nand_146 (nand_146_out, nand_137_out, nand_137_out);
  nand nand_147 (nand_147_out, nand_138_out, nand_138_out);
  nand nand_148 (nand_148_out, nand_139_out, nand_139_out);
  nand nand_149 (a_2, nand_141_out, nand_142_out);
  nand nand_150 (b_2, nand_143_out, nand_144_out);
  nand nand_151 (d_2, nand_145_out, nand_146_out);
  nand nand_152 (f, nand_147_out, nand_148_out);
endmodule

module display (
  input  [3:0] \input 
);

  wire n7segment_hex_decoder_1_a_2, n7segment_hex_decoder_1_b_2, n7segment_hex_decoder_1_c_2,
       n7segment_hex_decoder_1_d_2, n7segment_hex_decoder_1_e, n7segment_hex_decoder_1_g;

  _7segment_hex_decoder u_7segment_hex_decoder_1 (
    .D(\input [3]), .C(\input [2]), .B(\input [1]), .A(\input [0]), .a_2(n7segment_hex_decoder_1_a_2),
    .b_2(n7segment_hex_decoder_1_b_2), .c_2(n7segment_hex_decoder_1_c_2), .d_2(n7segment_hex_decoder_1_d_2),
    .e(n7segment_hex_decoder_1_e), .f(n7segment_hex_decoder_1_a_2), .g(n7segment_hex_decoder_1_g));
  _7segment_hex_decoder u_7segment_hex_decoder_2 ();  // open: D, C, B, A, a_2, b_2, c_2, d_2, e, f, g
  _7segment_hex_decoder u_7segment_hex_decoder_3 ();  // open: D, C, B, A, a_2, b_2, c_2, d_2, e, f, g
  Comparator #(.width(4)) comparator_1 ();  // open: a, b, gt, eq, lt
  _7_Segment_Display u_7_segment_display_1 (
    .g(n7segment_hex_decoder_1_g), .f(n7segment_hex_decoder_1_a_2), .a(n7segment_hex_decoder_1_a_2),
    .b(n7segment_hex_decoder_1_b_2), .e(n7segment_hex_decoder_1_e), .d(n7segment_hex_decoder_1_d_2),
    .c(n7segment_hex_decoder_1_c_2));  // open: dp
  _7_Segment_Display u_7_segment_display_2 (
    .g(n7segment_hex_decoder_1_g), .f(n7segment_hex_decoder_1_a_2), .a(n7segment_hex_decoder_1_a_2),
    .b(n7segment_hex_decoder_1_b_2), .e(n7segment_hex_decoder_1_e), .d(n7segment_hex_decoder_1_d_2),
    .c(n7segment_hex_decoder_1_c_2));  // open: dp
  _7_Segment_Display u_7_segment_display_3 (
    .g(n7segment_hex_decoder_1_g), .f(n7segment_hex_decoder_1_a_2), .a(n7segment_hex_decoder_1_a_2),
    .b(n7segment_hex_decoder_1_b_2), .e(n7segment_hex_decoder_1_e), .d(n7segment_hex_decoder_1_d_2),
    .c(n7segment_hex_decoder_1_c_2));  // open: dp
  _7_Segment_Display u_7_segment_display_4 (
    .g(n7segment_hex_decoder_1_g), .f(n7segment_hex_decoder_1_a_2), .a(n7segment_hex_decoder_1_a_2),
    .b(n7segment_hex_decoder_1_b_2), .e(n7segment_hex_decoder_1_e), .d(n7segment_hex_decoder_1_d_2),
    .c(n7segment_hex_decoder_1_c_2));  // open: dp
endmodule

// 8bitbinarydecoder
module _8bitbinarydecode (
  input  [7:0] \input ,
  output [3:0] output1,
  output [3:0] output2,
  output [3:0] output3
);

  wire comparativeadder_1_out_5, comparativeadder_1_out_6, comparativeadder_1_out_7,
       comparativeadder_1_out_8, comparativeadder_2_out_5, comparativeadder_2_out_6,
       comparativeadder_2_out_7, comparativeadder_2_out_8, comparativeadder_3_out_5,
       comparativeadder_3_out_6, comparativeadder_3_out_7, comparativeadder_3_out_8,
       comparativeadder_4_out_5, comparativeadder_4_out_6, comparativeadder_4_out_7,
       comparativeadder_4_out_8, comparativeadder_5_out_5, comparativeadder_5_out_6, comparativeadder_5_out_7;

  comparativeadder comparativeadder_1 (
    .in_1(\input [5]), .in_2(\input [6]), .in_3(\input [7]), .in_4(1'b0), .out_5(comparativeadder_1_out_5),
    .out_6(comparativeadder_1_out_6), .out_7(comparativeadder_1_out_7), .out_8(comparativeadder_1_out_8));
  comparativeadder comparativeadder_2 (
    .in_1(\input [4]), .in_2(comparativeadder_1_out_5), .in_3(comparativeadder_1_out_6),
    .in_4(comparativeadder_1_out_7), .out_5(comparativeadder_2_out_5), .out_6(comparativeadder_2_out_6),
    .out_7(comparativeadder_2_out_7), .out_8(comparativeadder_2_out_8));
  comparativeadder comparativeadder_3 (
    .in_1(\input [3]), .in_2(comparativeadder_2_out_5), .in_3(comparativeadder_2_out_6),
    .in_4(comparativeadder_2_out_7), .out_5(comparativeadder_3_out_5), .out_6(comparativeadder_3_out_6),
    .out_7(comparativeadder_3_out_7), .out_8(comparativeadder_3_out_8));
  comparativeadder comparativeadder_4 (
    .in_1(\input [2]), .in_2(comparativeadder_3_out_5), .in_3(comparativeadder_3_out_6),
    .in_4(comparativeadder_3_out_7), .out_5(comparativeadder_4_out_5), .out_6(comparativeadder_4_out_6),
    .out_7(comparativeadder_4_out_7), .out_8(comparativeadder_4_out_8));
  comparativeadder comparativeadder_5 (
    .in_1(comparativeadder_3_out_8), .in_2(comparativeadder_2_out_8), .in_3(comparativeadder_1_out_8),
    .in_4(1'b0), .out_5(comparativeadder_5_out_5), .out_6(comparativeadder_5_out_6),
    .out_7(comparativeadder_5_out_7), .out_8(output3[1]));
  comparativeadder comparativeadder_6 (
    .in_1(\input [1]), .in_2(comparativeadder_4_out_5), .in_3(comparativeadder_4_out_6),
    .in_4(comparativeadder_4_out_7), .out_5(output1[1]), .out_6(output1[2]), .out_7(output1[3]),
    .out_8(output2[0]));
  comparativeadder comparativeadder_7 (
    .in_1(comparativeadder_4_out_8), .in_2(comparativeadder_5_out_5), .in_3(comparativeadder_5_out_6),
    .in_4(comparativeadder_5_out_7), .out_5(output2[1]), .out_6(output2[2]), .out_7(output2[3]),
    .out_8(output3[0]));
  Hex_Digit_Display hex_digit_display_1 (.value({2'b00, output3[1:0]}));  // open: dp
  Hex_Digit_Display hex_digit_display_2 (.value(output2));  // open: dp
  Hex_Digit_Display hex_digit_display_3 (.value({output1[3:1], \input [0]}));  // open: dp

  assign output1[0] = \input [0];
  assign output3[3:2] = 2'b00;
endmodule

module _4_bit_adder (
  input  in_1,
  input  in_2,
  input  in_3,
  input  in_4,
  output out_5,
  output out_6,
  output out_7,
  output out_8
);

  wire and_1_out, and_2_out, and_3_out, and_4_out, and_5_out, or_1_out, or_2_out, xor_2_out, xor_3_out,
       xor_4_out;

  xor xor_1 (out_5, 1'b1, in_1);
  and and_1 (and_1_out, 1'b1, in_1);
  xor xor_2 (xor_2_out, 1'b1, in_2);
  and and_2 (and_2_out, 1'b1, in_2);
  xor xor_3 (xor_3_out, 1'b0, in_3);
  and and_3 (and_3_out, 1'b0, in_3);
  xor xor_4 (xor_4_out, 1'b0, in_4);
  xor xor_5 (out_6, and_1_out, xor_2_out);
  and and_4 (and_4_out, xor_2_out, and_1_out);
  or or_1 (or_1_out, and_4_out, and_2_out);
  and and_5 (and_5_out, or_1_out, xor_3_out);
  xor xor_6 (out_7, or_1_out, xor_3_out);
  or or_2 (or_2_out, and_5_out, and_3_out);
  xor xor_7 (out_8, or_2_out, xor_4_out);
endmodule

module comparativeadder (
  input  in_1,
  input  in_2,
  input  in_3,
  input  in_4,
  output out_5,
  output out_6,
  output out_7,
  output out_8
);

  wire n4bitcomparator_1_out_5;
  wire [3:0] n4_bit_adder_1_out_5;

  _4_bit_adder u_4_bit_adder_1 (
    .in_1(in_1), .in_2(in_2), .in_3(in_3), .in_4(in_4), .out_5(n4_bit_adder_1_out_5[0]),
    .out_6(n4_bit_adder_1_out_5[1]), .out_7(n4_bit_adder_1_out_5[2]), .out_8(n4_bit_adder_1_out_5[3]));
  _4bitcomparator u_4bitcomparator_1 (
    .in_1(in_4), .in_2(in_3), .in_3(in_2), .in_4(in_1), .out_5(n4bitcomparator_1_out_5));
  Multiplexer #(.width(4)) multiplexer_1 (
    .in0({in_4, in_3, in_2, in_1}), .in1(n4_bit_adder_1_out_5), .out({out_8, out_7, out_6, out_5}),
    .sel(n4bitcomparator_1_out_5));  // open: en
endmodule

module _4bitcomparator (
  input  in_1,
  input  in_2,
  input  in_3,
  input  in_4,
  output out_5
);

  wire and_1_out, and_2_out, and_3_out, and_4_out, not_1_out, not_2_out, not_3_out, not_4_out, xnor_1_out,
       xnor_2_out, xnor_3_out;

  not not_1 (not_1_out, 1'b0);
  not not_2 (not_2_out, 1'b1);
  not not_3 (not_3_out, 1'b0);
  not not_4 (not_4_out, 1'b0);
  and and_1 (and_1_out, not_1_out, in_1);
  xnor xnor_1 (xnor_1_out, 1'b0, in_1);
  xnor xnor_2 (xnor_2_out, 1'b1, in_2);
  xnor xnor_3 (xnor_3_out, 1'b0, in_3);
  and and_2 (and_2_out, xnor_1_out, not_2_out, in_2);
  and and_3 (and_3_out, xnor_2_out, xnor_1_out, in_3, not_3_out);
  or or_1 (out_5, and_1_out, and_2_out, and_3_out, and_4_out);
  and and_4 (and_4_out, xnor_1_out, xnor_3_out, xnor_2_out, not_4_out, in_4);
endmodule

module output_register (
  input  preset,
  input  enable,
  input  clear,
  input  clock,
  input  [7:0] \input ,
  output [7:0] \output 
);

  D_Flip_Flop d_ff_1 (
    .clk(clock), .D(\input [0]), .Q(\output [0]), .preset(enable), .en(enable), .reset(clear));  // open: Qn
  D_Flip_Flop d_ff_2 (
    .clk(clock), .D(\input [1]), .Q(\output [1]), .preset(enable), .en(enable), .reset(clear));  // open: Qn
  D_Flip_Flop d_ff_3 (
    .clk(clock), .D(\input [2]), .Q(\output [2]), .preset(enable), .en(enable), .reset(clear));  // open: Qn
  D_Flip_Flop d_ff_4 (
    .clk(clock), .D(\input [3]), .Q(\output [3]), .preset(enable), .en(enable), .reset(clear));  // open: Qn
  D_Flip_Flop d_ff_5 (
    .clk(clock), .D(\input [4]), .Q(\output [4]), .preset(enable), .en(enable), .reset(clear));  // open: Qn
  D_Flip_Flop d_ff_6 (
    .clk(clock), .D(\input [5]), .Q(\output [5]), .preset(enable), .en(enable), .reset(clear));  // open: Qn
  D_Flip_Flop d_ff_7 (
    .clk(clock), .D(\input [6]), .Q(\output [6]), .preset(enable), .en(enable), .reset(clear));  // open: Qn
  D_Flip_Flop d_ff_8 (
    .clk(clock), .D(\input [7]), .Q(\output [7]), .preset(enable), .en(enable), .reset(clear));  // open: Qn

  assign preset = enable;
endmodule

module empy_instruction (
  input  [7:0] in_1,
  input  [7:0] in_2,
  output out_3
);

  wire or_2_out;
  wire [7:0] or_1_out;

  assign or_1_out = in_1 | in_2;  // OR_Gate or_1, 8 bits wide
  or or_2 (or_2_out, or_1_out[0], or_1_out[1], or_1_out[2], or_1_out[4], or_1_out[5], or_1_out[6], or_1_out[7], or_1_out[3]);
  not not_1 (out_3, or_2_out);
endmodule
